# Fritzing sketch circuit diagram v03 (saved by Fritzing 1.0.2b)
breadboards: 1

parts:
  MCU1 = Raspberry Pi Zero
  Mod1 = TMC2209 [package=THT]
  HC-SR04_Sensor_1 = HC-SR04 Ultrasonic Distance Sensor
  R1 = Resistor [tolerance=±5% power=0.25W resistance=330 package=THT]
  R2 = Resistor [tolerance=±5% power=0.25W resistance=470 package=THT]
  C1 = Electrolytic Capacitor [capacitance=47µF voltage=35V package="100 mil [THT, electrolytic]"]
  M3 = Stepper Motor - Bipolar
  S2 = Taiway 100-SP-X-T1 SPDT Miniature Toggle Switch [part_number=100-SP-X-T1-0-0-B1-M2 package=THT]
  S3 = Pushbutton [package="[THT]"]
  S4 = Pushbutton [package="[THT]"]
  VCC1 = 4 x AAA Battery Mount
  M2 = RioRand LM2596
  S5 = D2F-FL Omron Snap Action Limit Switch with Level

nets:
  VDD: MCU1.pin_2, MCU1.pin_4, Mod1.VDD, HC-SR04_Sensor_1.VCC
  GND: MCU1.pin_6, MCU1.pin_9, Mod1.GND, Mod1.EN, HC-SR04_Sensor_1.GND, R1.Pin_1, R2.Pin_0, R2.Pin_1, C1.+, VCC1.-, M2.Pin_2, S5.Pin_1
  N1: MCU1.pin_7, HC-SR04_Sensor_1.TRIG
  N2: Mod1.B2, M3.D
  N3: Mod1.B1, M3.B
  N4: Mod1.A1, M3.C
  N5: Mod1.A2, M3.A
  N6: Mod1.VM, C1.-, S2.L2, M2.Pin_1
  N7: HC-SR04_Sensor_1.ECHO, R1.Pin_0
  N8: S2.L1, VCC1.+
  N9: S3.Pin_1, S3.Pin_2
  N10: S3.Pin_3, S3.Pin_4
  N11: S4.Pin_1, S4.Pin_2
  N12: S4.Pin_3, S4.Pin_4

custom parts:
  TMC2209: TMC2209-LA stepper motor controller and driver. Supply voltage 4.75-28V Iphase up to 1.77A rms (2.5A peak)
  D2F-FL Omron Snap Action Limit Switch with Level: Snap action switch with stainless steel lever.
