# Fritzing sketch schematic v01 (saved by Fritzing 1.0.1rc)
breadboards: 1

parts:
  Raspberry_Pi1 = Raspberry Pi Zero
  JL012-13-5_1 = JL012-13-5.2 Lever (Limit) Switch SPDT + NO + NC [part_number=JL012-13-5.2]
  Pololu_A1 = Pololu A4988 [package=SO16]
  HC-SR04_Sensor_1 = HC-SR04 Ultrasonic Distance Sensor
  M2 = RioRand LM2596
  BATT1 = 4xAA Switchable Battery Pack w/Bare Wire
  M3 = Stepper Motor - Bipolar
  C1 = Electrolytic Capacitor [capacitance=1μF voltage=35V package="0405 [SMD, electrolytic]"]

nets:
  N1: Raspberry_Pi1.GIPO17, HC-SR04_Sensor_1.TRIG
  N2: Raspberry_Pi1.GIPO27, JL012-13-5_1.NO
  N3: Raspberry_Pi1.GIPO22, Pololu_A1.STEP
  N4: Raspberry_Pi1.GIPO12, Pololu_A1.MS3
  N5: Raspberry_Pi1.GIPO25, Pololu_A1.MS2
  N6: Raspberry_Pi1.GIPO24, Pololu_A1.MS1
  N7: Raspberry_Pi1.GIPO23, Pololu_A1.DIR
  N8: Raspberry_Pi1.GIPO18, HC-SR04_Sensor_1.ECHO
  N9: Raspberry_Pi1.GND, JL012-13-5_1.C
  N10: Pololu_A1.RESET, Pololu_A1.SLEEP
  N11: Pololu_A1.GND#8, HC-SR04_Sensor_1.GND, M2.Pin_4
  VDD: Pololu_A1.VDD, HC-SR04_Sensor_1.VCC, M2.Pin_3
  N12: Pololu_A1.1B, M3.D
  N13: Pololu_A1.1A, M3.B
  N14: Pololu_A1.2A, M3.C
  N15: Pololu_A1.2B, M3.A
  N16: Pololu_A1.GND#14, M2.Pin_1, BATT1.NEG, C1.-
  N17: Pololu_A1.VMOT, M2.Pin_2, BATT1.POS, C1.+

custom parts:
  Raspberry Pi Zero: The Raspberry Pi Zero is the latest single board computer to be released by the Raspberry Pi Foundation. It is the entry level model Raspberry Pi perfect for hobbyists, makers and industrial engineers looking to create solutions where small size and low power consumption are important. This is especially relevant for applications in the wearables space as well as up and coming applications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
  JL012-13-5.2 Lever (Limit) Switch SPDT + NO + NC: Micro Switch; Model No.: JL012-13.5-2; Actuator Action: Momentary; Actuator Type: Hinge Lever; Contact Configuration: 1NO, 1NC (SPDT) Temperature -25~65℃；Relative humidity: below 85%; Rate Voltage: 125V AC; Rated Current: 1A.
  4xAA Switchable Battery Pack w/Bare Wire: 4xAA Switchable Battery Pack with Bare Wire connection
