# Fritzing sketch schematic v02 (saved by Fritzing 1.0.2b)
breadboards: 1

parts:
  Pololu_A1 = Pololu A4988 [package=SO16]
  C1 = Electrolytic Capacitor [capacitance=100µF voltage=35V package="200 mil [THT, electrolytic]"]
  Raspberry_Pi1 = Raspberry Pi Zero
  HC-SR04_Sensor_1 = HC-SR04 Ultrasonic Distance Sensor
  JL012-13-5_1 = JL012-13-5.2 Lever (Limit) Switch SPDT + NO + NC [part_number=JL012-13-5.2]
  M1 = Stepper Motor - Bipolar
  M2 = RioRand LM2596
  F1 = FUSE [package=fuse_5mm]
  VCC1 = 4 x AAA Battery Mount
  S1 = Taiway 100-SP-X-T1 SPDT Miniature Toggle Switch [part_number=100-SP-X-T1-0-0-B1-M1 package=THT]

nets:
  N1: Pololu_A1.RESET, Pololu_A1.SLEEP
  N2: Pololu_A1.STEP, Raspberry_Pi1.GIPO21
  N3: Pololu_A1.DIR, Raspberry_Pi1.GIPO20
  GND: Pololu_A1.GND#8, Raspberry_Pi1.GND, HC-SR04_Sensor_1.GND, JL012-13-5_1.C
  VDD: Pololu_A1.VDD, Raspberry_Pi1.5V, HC-SR04_Sensor_1.VCC
  N4: Pololu_A1.1B, M1.D
  N5: Pololu_A1.1A, M1.B
  N6: Pololu_A1.2A, M1.C
  N7: Pololu_A1.2B, M1.A
  N8: Pololu_A1.GND#14, C1.+, M2.Pin_2, VCC1.-
  N9: Pololu_A1.VMOT, C1.-, M2.Pin_1, S1.L2
  N10: Raspberry_Pi1.GIPO17, HC-SR04_Sensor_1.TRIG
  N11: Raspberry_Pi1.GIPO16, JL012-13-5_1.NO
  N12: Raspberry_Pi1.GIPO18, HC-SR04_Sensor_1.ECHO
  N13: F1.1, S1.L1

custom parts:
  Raspberry Pi Zero: The Raspberry Pi Zero is the latest single board computer to be released by the Raspberry Pi Foundation. It is the entry level model Raspberry Pi perfect for hobbyists, makers and industrial engineers looking to create solutions where small size and low power consumption are important. This is especially relevant for applications in the wearables space as well as up and coming applications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
  JL012-13-5.2 Lever (Limit) Switch SPDT + NO + NC: Micro Switch; Model No.: JL012-13.5-2; Actuator Action: Momentary; Actuator Type: Hinge Lever; Contact Configuration: 1NO, 1NC (SPDT) Temperature -25~65℃；Relative humidity: below 85%; Rate Voltage: 125V AC; Rated Current: 1A.
